# Fritzing sketch google-plant (saved by Fritzing 0.9.5d)
breadboards: 1

parts:
  U1 = ESP32-38PinWide [part_number=ESP32-38PinWide]
  R1 = Photocell (LDR) [package=THT]
  J1 = male pin header, 3 pins [form="♂ (male)"]
  R2 = Resistor [tolerance=±5% resistance=10k package=THT]
  Capacitive_Soil_Moisture_Sensor1 = DFRobot Capacitive Soil Moisture Sensor V1.0 [part_number=SEN0193]
  Part1 = KY-016 RGB Full Color LED Module [package="Breakout board"]

nets:
  N1: U1.GPIO39, J1.pin1, Capacitive_Soil_Moisture_Sensor1.A
  GND: U1.GPIO33, U1.GPIO26, U1.GND, J1.pin3, R2.Pin_0, Capacitive_Soil_Moisture_Sensor1.GND, Part1.-
  N2: U1.GPIO27, Part1.B
  N3: U1.GPIO14, Part1.G
  N4: U1.GPIO12, R1.pin_0, J1.pin2, Capacitive_Soil_Moisture_Sensor1.VCC
  N5: U1.GPIO10, U1.GPIO23
  N6: U1.GPIO8, U1.GPIO22
  N7: R1.pin_1, R2.Pin_1

notes:
  RGB Pins might be swapped
  R: G12
  G: G14
  B: G27
  Config Interrupt Pin: G33 -> GND

custom parts:
  ESP32-38PinWide: Generic 38-Pin ESP32 with wide format (only access to one side of pins on a breadboard) based on Stephen Lilley's HiLetgo ESP-WROOM-32 ESP32 ESP-32S Development Board.
  DFRobot Capacitive Soil Moisture Sensor V1.0: DFRobot Capacitive Soil Moisture Sensor V1.0 This product measures soil moisture levels by capacitive sensing, rather than resistive sensing like other types of moisture sensor. It is made of a corrosion resistant material giving it a long service life. Insert it into soil and impress your friends with the real-time soil moisture data! The product includes an on-board voltage regulator which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
  KY-016 RGB Full Color LED Module: KY-016 Arduino full color 5mm RGB LED, different colors can be obtained by mixing the three primary colors.
